# Fritzing sketch BoxBeatsSpectrum (saved by Fritzing 0.9.2b)

parts:
  Part1 = Arduino Uno (Rev3)  # not connected
  Part2 = SparkFun Spectrum Shield [part_number=DEV-13116]
  NEOPIXEL1 = Neopixel Strip -- White (60/m)
  NEOPIXEL2 = Neopixel Strip -- White (60/m)

nets:
  N1: Part2.D3, NEOPIXEL2.+5V
  N2: Part2.VIN, NEOPIXEL1.DI, NEOPIXEL2.DI
  GND: Part2.GND, NEOPIXEL1.GND, NEOPIXEL2.GND
  N3: Part2.D6, NEOPIXEL1.+5V

custom parts:
  SparkFun Spectrum Shield: This shield can be used to create sound visualizers, detect patterns in music or add sound activation to your microcontroller projects.
  Neopixel Strip -- White (60/m): Neopixel Strip, White, 60 pixels per meter.
